// Logisim project CPU Project.circ as structural Verilog: 2 circuits, main circuit main
module main (
);

  Multiplexer multiplexer_1 ();  // open: in0, in1, out, sel, en
endmodule

module ALU32 (
  input  [4:0] Sa__5,
  input  [31:0] Input__32,
  input  [3:0] Op__4
);
endmodule
