// Logisim project CPU.circ as structural Verilog: 1 circuit, main circuit CPU
module CPU (
  input  in_1,
  input  Clock
);

  wire Execute_p9, not_1_out, not_2_out;
  wire [3:0] Decode_opcode, Execute_p15, ID_EX_opcode_2;
  wire [4:0] Decode_rd, Decode_rt, Decode_shift, Execute_p16, Execute_p17, Fetch_clock_2, ID_EX_clock_data_2,
       ID_EX_rd_2, ID_EX_rt_2, ID_EX_shift_2, IF_ID_clock_data_2;
  wire [15:0] Decode_immediate, ID_EX_immediate_2;
  wire [31:0] Decode_a, Decode_b, Execute_p11, Execute_p12, Execute_p13, Execute_p14, Fetch_instructions,
       ID_EX_a_2, ID_EX_b_2, IF_ID_instructions_data_2, undriven;

  Fetch Fetch (.Clock(not_1_out), .Instructions(Fetch_instructions), .Clock_2(Fetch_clock_2));
  not not_1 (not_1_out, Clock);
  Decode Decode (
    .D(undriven), .Instruction(IF_ID_instructions_data_2), .Clock(not_2_out), .OpCode(Decode_opcode),
    .Shift(Decode_shift), .A(Decode_a), .B(Decode_b), .Immediate(Decode_immediate), .RT(Decode_rt),
    .RD(Decode_rd));
  IF_ID IF_ID (
    .Instructions_Data(Fetch_instructions), .Clock_Data(Fetch_clock_2), .Clock(Clock),
    .Instructions_Data_2(IF_ID_instructions_data_2), .Clock_Data_2(IF_ID_clock_data_2));
  not not_2 (not_2_out, Clock);
  ID_EX ID_EX (
    .OpCode(Decode_opcode), .Shift(Decode_shift), .A(Decode_a), .B(Decode_b), .Immediate(Decode_immediate),
    .RT(Decode_rt), .RD(Decode_rd), .Clock_Data(IF_ID_clock_data_2), .Clock(Clock),
    .OpCode_2(ID_EX_opcode_2), .Shift_2(ID_EX_shift_2), .A_2(ID_EX_a_2), .B_2(ID_EX_b_2),
    .Immediate_2(ID_EX_immediate_2), .RT_2(ID_EX_rt_2), .RD_2(ID_EX_rd_2), .Clock_Data_2(ID_EX_clock_data_2));
  // Execute Execute: pin names not known; wires that end beside it: ID_EX_opcode_2, ID_EX_shift_2, ID_EX_a_2, ID_EX_b_2, ID_EX_immediate_2, ID_EX_rt_2, ID_EX_rd_2, ID_EX_clock_data_2, Execute_p9, in_1, Execute_p11, Execute_p12, Execute_p13, Execute_p14, Execute_p15, Execute_p16, Execute_p17
  not not_3 (Execute_p9, Clock);
  EX_MEM EX_MEM (
    .A(Execute_p11), .D(Execute_p12), .B(Execute_p13), .Target(Execute_p14), .OpCode(Execute_p15),
    .RT(Execute_p16), .RD(Execute_p17), .Clock(Clock));  // open: A_2, D_2, B_2, Target_2, OpCode_2, RT_2, RD_2
endmodule
